// Logisim project 1.circ as structural Verilog: 1 circuit, main circuit main
module main (
  input  A,
  input  B,
  input  C_in,
  output Sum,
  output C_out
);

  wire AND_2_out, AND_out, XOR_out;

  xor XOR (XOR_out, A, B);
  and AND (AND_out, A, B);
  xor XOR_2 (Sum, XOR_out, C_in);
  and AND_2 (AND_2_out, XOR_out, C_in);
  or OR (C_out, AND_2_out, AND_out);
endmodule
