// Logisim project 8bit_ALU_Logisim(2).circ as structural Verilog: 1 circuit, main circuit main
module main (
  input  [7:0] A_7_0,
  input  [7:0] B_7_0,
  input  [2:0] Opcode_2_0,
  input  Cin,
  output [7:0] Result_7_0,
  output Zero__Z,
  output Carry__C,
  output Overflow__V
);

  wire multiplexer_1_p1, multiplexer_1_p2, multiplexer_1_p3, multiplexer_1_p4, multiplexer_2_p1,
       multiplexer_2_p2, multiplexer_2_p3, multiplexer_3_p1, multiplexer_3_p2;
  wire [7:1] undriven;

  // Adder #(.width(8)) adder_1: pin names not known; wires that end beside it: A_7_0, B_7_0
  // Subtractor #(.width(8)) subtractor_1: pin names not known; wires that end beside it: A_7_0, B_7_0
  // Adder #(.width(8)) adder_2: pin names not known; wires that end beside it: A_7_0, B_7_0, Cin
  // Subtractor #(.width(8)) subtractor_2: pin names not known; wires that end beside it: Cin, A_7_0, B_7_0, Cin
  // AND_Gate #(.width(8)) and_1: pin names not known; wires that end beside it: A_7_0, B_7_0
  // OR_Gate #(.width(8)) or_1: pin names not known; wires that end beside it: A_7_0, B_7_0
  // XOR_Gate #(.width(8)) xor_1: pin names not known; wires that end beside it: A_7_0, B_7_0
  // Multiplexer #(.select(2), .width(8)) multiplexer_1: pin names not known; wires that end beside it: multiplexer_1_p1, multiplexer_1_p2, multiplexer_1_p3, multiplexer_1_p4, {Result_7_0[7:3], Opcode_2_0}
  // Multiplexer #(.select(2), .width(8)) multiplexer_2: pin names not known; wires that end beside it: multiplexer_2_p1, multiplexer_2_p2, multiplexer_2_p3, {Result_7_0[7:3], Opcode_2_0}
  // Multiplexer #(.select(1), .width(8)) multiplexer_3: pin names not known; wires that end beside it: multiplexer_3_p1, multiplexer_3_p2
  nor nor_1 (Zero__Z, undriven[1], undriven[2], undriven[3], undriven[4], undriven[6], undriven[7]);
  // Pins of 3 and 8 bits meet at {Result_7_0[7:3], Opcode_2_0}
  // Pins of 1 and 8 bits meet at {undriven, Zero__Z}

  assign Carry__C = 1'b0;
  assign Overflow__V = 1'b0;
  assign Result_7_0[2:0] = Opcode_2_0;

  // Notes on the sheet:
  //   ARITHMETIC UNIT
  //   000 ADD   001 SUB   010 ADC   011 SBB
  //   LOGIC UNIT
  //   100 AND   101 OR   110 XOR   111 = XOR
endmodule
